// Logisim project ex4.circ as structural Verilog: 5 circuits, main circuit RotRight
module RotRight (
  input  [15:0] INPUT0,
  input  [3:0] AMOUNT,
  output [15:0] OUTPUT0
);

  wire [15:0] r0, r1, r2, rot1_1_out_2, rot2_1_out_2, rot4_1_out_2, rot8_1_out_2;

  rot1 rot1_1 (.in_1(INPUT0), .out_2(rot1_1_out_2));
  rot2 rot2_1 (.in_1(r0), .out_2(rot2_1_out_2));
  rot4 rot4_1 (.in_1(r1), .out_2(rot4_1_out_2));
  rot8 rot8_1 (.in_1(r2), .out_2(rot8_1_out_2));
  Multiplexer #(.width(16)) multiplexer_1 (.in0(INPUT0), .in1(rot1_1_out_2), .out(r0), .sel(AMOUNT[0]));
  Multiplexer #(.width(16)) multiplexer_2 (.in0(r0), .in1(rot2_1_out_2), .out(r1), .sel(AMOUNT[1]));
  Multiplexer #(.width(16)) multiplexer_3 (.in0(r1), .in1(rot4_1_out_2), .out(r2), .sel(AMOUNT[2]));
  Multiplexer #(.width(16)) multiplexer_4 (.in0(r2), .in1(rot8_1_out_2), .out(OUTPUT0), .sel(AMOUNT[3]));

  // Other names for the same wires on the sheet: b0 = AMOUNT[0]; b1 = AMOUNT[1]; b2 = AMOUNT[2]; b3 = AMOUNT[3];
  //   r3[15:0] = OUTPUT0
endmodule

module rot1 (
  input  [15:0] in_1,
  output [15:0] out_2
);

  wire [15:0] bit_extender_1_out;

  assign bit_extender_1_out = {{1{1'b0}}, in_1[15:1]};  // Bit_Extender bit_extender_1
  assign out_2 = {in_1[0], {15{1'b0}}} | bit_extender_1_out;  // OR_Gate or_1, 16 bits wide
endmodule

module rot2 (
  input  [15:0] in_1,
  output [15:0] out_2
);

  wire [15:0] rot1_1_out_2;

  rot1 rot1_1 (.in_1(in_1), .out_2(rot1_1_out_2));
  rot1 rot1_2 (.in_1(rot1_1_out_2), .out_2(out_2));
endmodule

module rot4 (
  input  [15:0] in_1,
  output [15:0] out_2
);

  wire [15:0] rot2_1_out_2;

  rot2 rot2_1 (.in_1(in_1), .out_2(rot2_1_out_2));
  rot2 rot2_2 (.in_1(rot2_1_out_2), .out_2(out_2));
endmodule

module rot8 (
  input  [15:0] in_1,
  output [15:0] out_2
);

  wire [15:0] rot4_1_out_2;

  rot4 rot4_1 (.in_1(in_1), .out_2(rot4_1_out_2));
  rot4 rot4_2 (.in_1(rot4_1_out_2), .out_2(out_2));
endmodule
